// Logisim project Final_project_332.circ as structural Verilog
module main (
  input  [22:0] in_1,
  input  write_pc,
  output [22:0] out_3,
  output [22:0] Decimal,
  output [22:0] out_5,
  output [22:0] out_6,
  output [22:0] out_7,
  output [10:0] out_8,
  output [18:0] out_9,
  output [22:0] out_10
);

  wire Addi, ALU_SRC, Branch, button_1_out, EQ, eq_neq_1_select_output, Jump, Load, MemToReg, NEQ,
       Register_Dest, RegWrite, Store, timer_clock;
  wire [2:0] fun, multiplexer_5_out;
  wire [3:0] bit_extender_1_out, multiplexer_3_out, opcode, RD, RS, RT, Shift;
  wire [22:0] adder_1_out, adder_2_out, Address, multiplexer_1_out, multiplexer_2_out, ram_1_dout,
       register_1_q, register_file_1_out_8;

  Button button_1 (.out(button_1_out));
  Clock clock_1 (.out(timer_clock));
  Hex_Digit_Display hex_digit_display_1 (.value(bit_extender_1_out));  // open: dp
  Hex_Digit_Display hex_digit_display_2 (.value(Shift));  // open: dp
  assign bit_extender_1_out = {{1{fun[2]}}, fun};  // Bit_Extender bit_extender_1
  Register #(.width(23)) register_1 (
    .D(multiplexer_2_out), .en(write_pc), .clk(timer_clock), .Q(register_1_q), .clr(button_1_out));
  Hex_Digit_Display hex_digit_display_3 (.value(RD));  // open: dp
  Hex_Digit_Display hex_digit_display_4 (.value(RT));  // open: dp
  Immediate_Address immediate_address_1 (
    .func(fun), .Rs(RS), .Rt(RT), .Rd(RD), .shift(Shift), .out_8(out_8), .out_6(out_9), .out_9(out_10),
    .out_7(Address));
  Hex_Digit_Display hex_digit_display_5 (.value(RS));  // open: dp
  Hex_Digit_Display hex_digit_display_6 (.value(opcode));  // open: dp
  Adder #(.width(23)) adder_1 (.a(in_1), .b(register_1_q), .out(adder_1_out));  // open: cin, cout
  ROM #(.addrWidth(23), .dataWidth(23)) rom_1 (.addr(register_1_q), .data({fun, Shift, RD, RT, RS, opcode}));
  Multiplexer #(.width(23)) multiplexer_1 (
    .in0(adder_1_out), .in1(adder_2_out), .out(multiplexer_1_out), .sel(eq_neq_1_select_output));
  EQ_NEQ eq_neq_1 (.BEQ(EQ), .Control(Branch), .NEQ(NEQ), .select_output(eq_neq_1_select_output));
  Adder #(.width(23)) adder_2 (.a(adder_1_out), .b(out_10), .out(adder_2_out));  // open: cin, cout
  Hex_Digit_Display hex_digit_display_7 (.value(bit_extender_1_out));  // open: dp
  Hex_Digit_Display hex_digit_display_8 (.value(Shift));  // open: dp
  Hex_Digit_Display hex_digit_display_9 (.value(RD));  // open: dp
  Multiplexer #(.width(23)) multiplexer_2 (.in0(multiplexer_1_out), .in1(Address), .out(multiplexer_2_out), .sel(Jump));
  Hex_Digit_Display hex_digit_display_10 (.value(RT));  // open: dp
  Hex_Digit_Display hex_digit_display_11 (.value(RS));  // open: dp
  Hex_Digit_Display hex_digit_display_12 (.value(opcode));  // open: dp
  Multiplexer #(.width(4)) multiplexer_3 (.in0(RD), .in1(RT), .out(multiplexer_3_out), .sel(Register_Dest));
  Hex_Digit_Display hex_digit_display_13 (.value(bit_extender_1_out));  // open: dp
  ControlUnit controlunit_1 (
    .in_1(opcode), .Register_dest(Register_Dest), .Alu_src(ALU_SRC), .MemToReg(MemToReg),
    .Reg_write(RegWrite), .load(Load), .store(Store), .branch(Branch), .Jump(Jump), .out_10(Addi));
  Hex_Digit_Display hex_digit_display_14 (.value(Shift));  // open: dp
  Hex_Digit_Display hex_digit_display_15 (.value(RD));  // open: dp
  register_file register_file_1 (
    .WRITE_ENABLE(RegWrite), .in_5(RT), .in_4(RS), .REGISTER_SELECT(multiplexer_3_out), .in_2(Decimal),
    .CLOCK(timer_clock), .out_8(register_file_1_out_8), .out_7(out_5));
  Hex_Digit_Display hex_digit_display_16 (.value(RT));  // open: dp
  Hex_Digit_Display hex_digit_display_17 (.value(RS));  // open: dp
  Multiplexer #(.width(23)) multiplexer_4 (.in0(register_file_1_out_8), .in1(out_10), .out(out_6), .sel(ALU_SRC));
  Hex_Digit_Display hex_digit_display_18 (.value(opcode));  // open: dp
  Multiplexer #(.width(3)) multiplexer_5 (.in0(fun), .in1(3'b011), .out(multiplexer_5_out), .sel(Addi));
  ALU alu_1 (
    .in_2(out_5), .shift_bits(Shift), .in_1(out_6), .alu_select(multiplexer_5_out), .Equal(EQ),
    .Not_Equal(NEQ), .out_5(out_7));  // open: Cout
  RAM #(.addrWidth(23), .asyncread("true"), .dataWidth(23)) ram_1 (
    .addr(out_7), .we(Store), .oe(Load), .clk(timer_clock), .din(register_file_1_out_8), .dout(ram_1_dout));
  Multiplexer #(.width(23)) multiplexer_6 (.in0(out_7), .in1(ram_1_dout), .out(Decimal), .sel(MemToReg));

  assign out_3 = Decimal;

  // Other names for the same wires on the sheet: Data[22:0] = Decimal; Immediate[22:0] = out_10

  // Notes on the sheet:
  //   Reset_pc
  //   CLK
  //   R-Type
  //   Shft
  //   Fun
  //   Rd
  //   Rt
  //   PC
  //   Rs
  //   Opcode
  //   contents of rom_1 (hex, n*v repeats v):
  //   1101 a201 a01 1301 30aa10 301130 704210 4404 a03
  //   I-Type
  //   branch
  //   Instruction Memory
  //   --Immediate--
  //   jump
  //   Rt
  //   Rs
  //   Opcode
  //   23 Bits MIPS Single Cycle CPU
  //   J-Type
  //   ------Address------
  //   Opcode
  //   Data  To Write In Memory
  //   Data Output :
endmodule

module register_file (
  input  [3:0] REGISTER_SELECT,
  input  [22:0] in_2,
  input  WRITE_ENABLE,
  input  [3:0] in_4,
  input  [3:0] in_5,
  input  CLOCK,
  output [22:0] out_7,
  output [22:0] out_8
);

  wire and_1_out, and_2_out, and_3_out, and_4_out, and_5_out, and_6_out, and_7_out, and_8_out, and_9_out,
       and_10_out, and_11_out, and_12_out, and_13_out, and_14_out, and_15_out, and_16_out, decoder_1_out0,
       decoder_1_out1, decoder_1_out2, decoder_1_out3, decoder_1_out4, decoder_1_out5, decoder_1_out6,
       decoder_1_out7, decoder_1_out8, decoder_1_out9, decoder_1_out10, decoder_1_out11, decoder_1_out12,
       decoder_1_out13, decoder_1_out14, decoder_1_out15;
  wire [22:0] R0, R1, R2, R3, R4, R5, R6, R7, R8, R9, R10, R11, R12, R13, R14, R15;

  and and_1 (and_1_out, WRITE_ENABLE, decoder_1_out0);
  and and_2 (and_2_out, WRITE_ENABLE, decoder_1_out1);
  and and_3 (and_3_out, WRITE_ENABLE, decoder_1_out2);
  and and_4 (and_4_out, WRITE_ENABLE, decoder_1_out3);
  and and_5 (and_5_out, WRITE_ENABLE, decoder_1_out4);
  and and_6 (and_6_out, WRITE_ENABLE, decoder_1_out5);
  and and_7 (and_7_out, WRITE_ENABLE, decoder_1_out6);
  and and_8 (and_8_out, WRITE_ENABLE, decoder_1_out7);
  Decoder #(.select(4)) decoder_1 (
    .out0(decoder_1_out0), .out1(decoder_1_out1), .out2(decoder_1_out2), .out3(decoder_1_out3),
    .out4(decoder_1_out4), .out5(decoder_1_out5), .out6(decoder_1_out6), .out7(decoder_1_out7),
    .out8(decoder_1_out8), .out9(decoder_1_out9), .out10(decoder_1_out10), .out11(decoder_1_out11),
    .out12(decoder_1_out12), .out13(decoder_1_out13), .out14(decoder_1_out14), .out15(decoder_1_out15),
    .sel(REGISTER_SELECT));  // open: en
  Register #(.width(23)) register_1 (.D(in_2), .en(and_1_out), .clk(CLOCK), .Q(R0));  // open: clr
  Register #(.width(23)) register_2 (.D(in_2), .en(and_2_out), .clk(CLOCK), .Q(R1));  // open: clr
  Register #(.width(23)) register_3 (.D(in_2), .en(and_3_out), .clk(CLOCK), .Q(R2));  // open: clr
  Register #(.width(23)) register_4 (.D(in_2), .en(and_4_out), .clk(CLOCK), .Q(R3));  // open: clr
  Register #(.width(23)) register_5 (.D(in_2), .en(and_5_out), .Q(R4));  // open: clk, clr
  Register #(.width(23)) register_6 (.D(in_2), .en(and_6_out), .clk(CLOCK), .Q(R5));  // open: clr
  Register #(.width(23)) register_7 (.D(in_2), .en(and_7_out), .clk(CLOCK), .Q(R6));  // open: clr
  Register #(.width(23)) register_8 (.D(in_2), .en(and_8_out), .clk(CLOCK), .Q(R7));  // open: clr
  and and_9 (and_9_out, WRITE_ENABLE, decoder_1_out8);
  and and_10 (and_10_out, WRITE_ENABLE, decoder_1_out9);
  and and_11 (and_11_out, WRITE_ENABLE, decoder_1_out10);
  and and_12 (and_12_out, WRITE_ENABLE, decoder_1_out11);
  and and_13 (and_13_out, WRITE_ENABLE, decoder_1_out12);
  and and_14 (and_14_out, WRITE_ENABLE, decoder_1_out13);
  and and_15 (and_15_out, WRITE_ENABLE, decoder_1_out14);
  and and_16 (and_16_out, WRITE_ENABLE, decoder_1_out15);
  Register #(.width(23)) register_9 (.D(in_2), .en(and_9_out), .clk(CLOCK), .Q(R8));  // open: clr
  Register #(.width(23)) register_10 (.D(in_2), .en(and_10_out), .clk(CLOCK), .Q(R9));  // open: clr
  Register #(.width(23)) register_11 (.D(in_2), .en(and_11_out), .clk(CLOCK), .Q(R10));  // open: clr
  Register #(.width(23)) register_12 (.D(in_2), .en(and_12_out), .clk(CLOCK), .Q(R11));  // open: clr
  Register #(.width(23)) register_13 (.D(in_2), .en(and_13_out), .clk(CLOCK), .Q(R12));  // open: clr
  Register #(.width(23)) register_14 (.D(in_2), .en(and_14_out), .clk(CLOCK), .Q(R13));  // open: clr
  Register #(.width(23)) register_15 (.D(in_2), .en(and_15_out), .clk(CLOCK), .Q(R14));  // open: clr
  Register #(.width(23)) register_16 (.D(in_2), .en(and_16_out), .clk(CLOCK), .Q(R15));  // open: clr
  Multiplexer #(.select(4), .width(23)) multiplexer_1 (
    .in0(R0), .in1(R1), .in2(R2), .in3(R3), .in4(R4), .in5(R5), .in6(R6), .in7(R7), .in8(R8), .in9(R9),
    .in10(R10), .in11(R11), .in12(R12), .in13(R13), .in14(R14), .in15(R15), .out(out_7), .sel(in_4));
  Multiplexer #(.select(4), .width(23)) multiplexer_2 (
    .in0(R0), .in1(R1), .in2(R2), .in3(R3), .in4(R4), .in5(R5), .in6(R6), .in7(R7), .in8(R8), .in9(R9),
    .in10(R10), .in11(R11), .in12(R12), .in13(R13), .in14(R14), .in15(R15), .out(out_8), .sel(in_5));

  // Notes on the sheet:
  //   WRITE DATA
  //   RD
  //   R0
  //   R1
  //   R2
  //   R3
  //   R4
  //   R5
  //   R6
  //   R7
  //   R8
  //   R9
  //   R10
  //   R11
  //   R12
  //   R13
  //   R14
  //   R15
  //   RS
  //   RT
  //   READ DATA-1
  //   READ DATA-2
endmodule

module alu_1bit (
  input  A,
  input  B,
  input  Cin,
  input  [1:0] MUX_select,
  output Result,
  output cout
);

  wire adder_1_out, and_1_out, multiplexer_1_out, nor_1_out, not_1_out, or_1_out;

  Multiplexer multiplexer_1 (.in0(B), .in1(not_1_out), .out(multiplexer_1_out), .sel(Cin));
  not not_1 (not_1_out, B);
  or or_1 (or_1_out, B, A);
  nor nor_1 (nor_1_out, B, A);
  and and_1 (and_1_out, B, A);
  Adder #(.width(1)) adder_1 (.a(multiplexer_1_out), .b(A), .out(adder_1_out), .cin(Cin), .cout(cout));
  Multiplexer #(.select(2)) multiplexer_2 (
    .in0(or_1_out), .in1(and_1_out), .in2(nor_1_out), .in3(adder_1_out), .out(Result), .sel(MUX_select));
endmodule

module ALU (
  input  [22:0] in_1,
  input  [22:0] in_2,
  input  [2:0] alu_select,
  input  [3:0] shift_bits,
  output [22:0] out_5,
  output Cout,
  output Equal,
  output Not_Equal
);

  wire comparator_1_gt, comparator_1_lt;
  wire [4:0] bit_extender_1_out;
  wire [22:0] adder_1_out, and_1_out, multiplexer_1_out, multiplexer_2_out, nor_1_out, not_1_out, or_1_out,
       shifter_1_out, shifter_2_out;

  assign not_1_out = ~in_1;  // NOT_Gate not_1, 23 bits wide
  assign bit_extender_1_out = {{1{shift_bits[3]}}, shift_bits};  // Bit_Extender bit_extender_1
  assign or_1_out = in_2 | in_1;  // OR_Gate or_1, 23 bits wide
  assign nor_1_out = ~(in_2 | in_1);  // NOR_Gate nor_1, 23 bits wide
  assign and_1_out = in_2 & in_1;  // AND_Gate and_1, 23 bits wide
  Multiplexer #(.width(23)) multiplexer_1 (.in0(in_1), .in1(not_1_out), .out(multiplexer_1_out), .sel(alu_select[2]));
  Comparator #(.width(23)) comparator_1 (.a(in_1), .b(in_2), .gt(comparator_1_gt), .eq(Equal), .lt(comparator_1_lt));
  Adder #(.width(23)) adder_1 (.a(in_2), .b(multiplexer_1_out), .out(adder_1_out), .cin(alu_select[2]), .cout(Cout));
  Shifter #(.width(23)) shifter_1 (.in(in_2), .\dist (bit_extender_1_out), .out(shifter_1_out));
  Shifter #(.shift("lr"), .width(23)) shifter_2 (.in(in_2), .\dist (bit_extender_1_out), .out(shifter_2_out));
  or or_2 (Not_Equal, comparator_1_gt, comparator_1_lt);
  Multiplexer #(.width(23)) multiplexer_2 (
    .in0({23{1'b0}}), .in1(23'h1), .out(multiplexer_2_out), .sel(comparator_1_lt));
  Multiplexer #(.select(3), .width(23)) multiplexer_3 (
    .in0(or_1_out), .in1(nor_1_out), .in2(and_1_out), .in3(adder_1_out), .in4(adder_1_out),
    .in5(shifter_1_out), .in6(shifter_2_out), .in7(multiplexer_2_out), .out(out_5), .sel(alu_select));

  // Notes on the sheet:
  //   A
  //   Cin
  //   B
  //   OR
  //   AND
  //   NOR
  //   LLS
  //   LRS
  //   ADD/SUB
  //   SLT
  //   Result
endmodule

module Data_path (
  input  [22:0] in_1,
  input  in_2,
  input  in_3,
  output [2:0] Func,
  output [3:0] Shift,
  output [3:0] Rd,
  output [3:0] Rt,
  output [3:0] Rs,
  output [3:0] Opcode,
  output [22:0] out_10,
  output out_11
);

  wire alu_1_p7, alu_1_p8, and_1_out, and_2_out, clock_1_out, or_1_out, undriven, undriven_2, undriven_3,
       undriven_4, undriven_5, undriven_6, undriven_7, undriven_9, undriven_10;
  wire [2:0] multiplexer_3_out, undriven_8;
  wire [3:0] multiplexer_1_out;
  wire [22:0] adder_1_out, adder_2_out, alu_1_p5, bit_extender_1_out, bit_extender_2_out, multiplexer_2_out,
       multiplexer_4_out, multiplexer_5_out, ram_1_dout, register_1_q, register_file_1_out_7,
       register_file_1_out_8;

  Register #(.width(23)) register_1 (.D(multiplexer_5_out), .en(in_2), .clk(clock_1_out), .Q(register_1_q), .clr(in_3));
  Clock clock_1 (.out(clock_1_out));
  Adder #(.width(23)) adder_1 (.a(in_1), .b(register_1_q), .out(adder_1_out));  // open: cin, cout
  ROM #(.addrWidth(23), .dataWidth(23)) rom_1 (.addr(register_1_q), .data({Opcode, Rs, Rt, Rd, Shift, Func}));
  // ControlUnit controlunit_1: pin names not known; wires that end beside it: Opcode, Func
  Multiplexer #(.width(4)) multiplexer_1 (.in0(Rd), .in1(Rt), .out(multiplexer_1_out), .sel(undriven_9));
  assign bit_extender_1_out = {{12{Func[2]}}, {Func, Shift, Rd}};  // Bit_Extender bit_extender_1
  register_file register_file_1 (
    .WRITE_ENABLE(undriven_2), .in_5(Rt), .in_4(Rs), .REGISTER_SELECT(multiplexer_1_out), .in_2(out_10),
    .CLOCK(clock_1_out), .out_8(register_file_1_out_8), .out_7(register_file_1_out_7));
  Multiplexer #(.width(23)) multiplexer_2 (
    .in0(register_file_1_out_8), .in1(bit_extender_1_out), .out(multiplexer_2_out), .sel(undriven_10));
  Multiplexer #(.width(3)) multiplexer_3 (.in0(Func), .in1(undriven_8), .out(multiplexer_3_out), .sel(undriven_7));
  Adder #(.width(23)) adder_2 (.a(adder_1_out), .b(bit_extender_1_out), .out(adder_2_out));  // open: cin, cout
  // ALU alu_1: pin names not known; wires that end beside it: register_file_1_out_7, multiplexer_2_out, Rs, multiplexer_3_out, alu_1_p5, out_11, alu_1_p7, alu_1_p8
  or or_1 (or_1_out, and_1_out, and_2_out);
  and and_1 (and_1_out, alu_1_p7, undriven_5);
  Multiplexer #(.width(23)) multiplexer_4 (
    .in0(adder_1_out), .in1(adder_2_out), .out(multiplexer_4_out), .sel(or_1_out));
  and and_2 (and_2_out, alu_1_p8, undriven_5);
  assign bit_extender_2_out = {{4{Opcode[3]}}, {Opcode, Rs, Rt, Rd, Shift[3:1]}};  // Bit_Extender bit_extender_2
  RAM #(.addrWidth(23), .asyncread("true"), .dataWidth(23)) ram_1 (
    .addr(alu_1_p5), .we(undriven_4), .oe(undriven_3), .clk(clock_1_out), .din(multiplexer_2_out),
    .dout(ram_1_dout));
  Multiplexer #(.width(23)) multiplexer_5 (
    .in0(multiplexer_4_out), .in1(bit_extender_2_out), .out(multiplexer_5_out), .sel(undriven_6));
  Multiplexer #(.width(23)) multiplexer_6 (.in0(alu_1_p5), .in1(ram_1_dout), .out(out_10), .sel(undriven));

  // Notes on the sheet:
  //   contents of rom_1 (hex, n*v repeats v):
  //   100800 180801
  //   Result
endmodule

module ControlUnit (
  input  [3:0] in_1,
  output Register_dest,
  output Alu_src,
  output MemToReg,
  output Reg_write,
  output load,
  output store,
  output branch,
  output Jump,
  output out_10
);

  wire decoder_1_out0, decoder_1_out1, decoder_1_out4, decoder_1_out5, decoder_1_out7, decoder_1_out8,
       decoder_1_out9, decoder_1_out10, decoder_1_out11, decoder_1_out12, decoder_1_out13, decoder_1_out14,
       decoder_1_out15;

  Decoder #(.select(4)) decoder_1 (
    .out0(decoder_1_out0), .out1(decoder_1_out1), .out2(load), .out3(store), .out4(decoder_1_out4),
    .out5(decoder_1_out5), .out6(Jump), .out7(decoder_1_out7), .out8(decoder_1_out8), .out9(decoder_1_out9),
    .out10(decoder_1_out10), .out11(decoder_1_out11), .out12(decoder_1_out12), .out13(decoder_1_out13),
    .out14(decoder_1_out14), .out15(decoder_1_out15), .sel(in_1));  // open: en
  or or_1 (Register_dest, decoder_1_out1, load, store, decoder_1_out4, decoder_1_out4);
  or or_2 (Alu_src, decoder_1_out1, load, store);
  or or_3 (Reg_write, decoder_1_out0, decoder_1_out1, load);
  or or_4 (branch, decoder_1_out4, decoder_1_out5);
  or or_5 (out_10, store, decoder_1_out1, load);

  assign MemToReg = load;

  // Notes on the sheet:
  //   Addi
endmodule

module EQ_NEQ (
  input  BEQ,
  input  Control,
  input  NEQ,
  output select_output
);

  wire and_1_out, and_2_out;

  and and_1 (and_1_out, BEQ, Control);
  or or_1 (select_output, and_1_out, and_2_out);
  and and_2 (and_2_out, Control, NEQ);
endmodule

module Immediate_Address (
  input  [3:0] Rs,
  input  [3:0] Rt,
  input  [3:0] Rd,
  input  [3:0] shift,
  input  [2:0] func,
  output [18:0] out_6,
  output [22:0] out_7,
  output [10:0] out_8,
  output [22:0] out_9
);

  assign out_7 = {{4{func[2]}}, {func, shift, Rd, Rt, Rs}};  // Bit_Extender bit_extender_1
  assign out_9 = {{12{func[2]}}, {func, shift, Rd}};  // Bit_Extender bit_extender_2

  assign out_6 = {func, shift, Rd, Rt, Rs};
  assign out_8 = {func, shift, Rd};

  // Notes on the sheet:
  //   Immediate
  //   Address
endmodule
